# Fritzing sketch Fritzing Schematic (saved by Fritzing 0.9.0b)
breadboards: 2

parts:
  Part1 = Arduino Uno (Rev3) - ICSP
  Part2 = Arduino Xbee Libellium Shield
  LCD1 = LCD screen
  M1 = Stepper Motor - Bipolar
  IC1 = L293D [package=THT]
  R1 = Rotary Potentiometer (Small) [maximum_resistance=100kΩ package=THT]
  S1 = Pushbutton [package="[THT]"]
  R2 = Resistor [tolerance=±5% resistance=1k package="0603 [SMD]"]
  R3 = Resistor [tolerance=±5% resistance=10k package="1206 [SMD]"]
  Q1 = NPN-Transistor [package="TO92 [THT]"]
  R4 = Resistor [package="2010 [SMD]"]
  Q2 = NPN-Transistor [package="TO92 [THT]"]
  R5 = Resistor [package="2010 [SMD]"]
  R6 = Resistor [tolerance=±5% resistance=10k package="1206 [SMD]"]
  Part3 = Gas Sensor Breakout Board

nets:
  N1: Part1.A0, Part3.B1
  N2: Part1.A1, S1.Pin_1, S1.Pin_2, R2.Pin_0
  N3: Part1.ICSP_MISO, Part1.D12/MISO, LCD1.RS
  N4: Part1.ICSP_MOSI, Part1.D11_PWM/MOSI, LCD1.E
  N5: Part1.D9_PWM, IC1.In_1, R4.Pin_0
  N6: Part1.D10_PWM/SS, IC1.In_4, R5.Pin_1
  GND: Part1.GND, Part2.GND, LCD1.VSS, LCD1.R/W, LCD1.LED-, IC1.0V, R1.leg2, R2.Pin_1, Q1.E, Q2.E, Part3.GND
  N7: Part1.D2, LCD1.DB7
  N8: Part1.D3_PWM, LCD1.DB6
  N9: Part1.D4, LCD1.DB5
  N10: Part1.D5_PWM, LCD1.DB4
  N11: Part1.D6_PWM, Part2.M8RXD
  N12: Part1.D7, Part2.M8TXD
  3V3: Part1.3V3, Part2.+3V3
  5V: Part1.5V, LCD1.VDD, LCD1.LED+, IC1.Enable_1, IC1.Enable_2, IC1.+V, R1.leg1, S1.Pin_3, S1.Pin_4, R3.Pin_1, R6.Pin_1, Part3.A1, Part3.H1
  N13: Part1.VIN, IC1.+Vmotor
  N14: LCD1.V0, R1.wiper
  N15: M1.A, IC1.Out_4_(_Controlled_by_Enable_2_)
  N16: M1.C, IC1.Out_1_(_Controlled_by_Enable_1_)
  N17: M1.B, IC1.Out_3_(_Controlled_by_Enable_2_)
  N18: M1.D, IC1.Out_2_(_Controlled_by_Enable_1_)
  N19: IC1.In_2, R3.Pin_0, Q1.C
  N20: IC1.In_3, Q2.C, R6.Pin_0
  N21: Q1.B, R4.Pin_1
  N22: Q2.B, R5.Pin_0
